// Logisim project Day10_Counters.circ as structural Verilog
module BasicLatch (
  input  Basic_Latch,
  output out_2
);

  or or_1 (out_2, Basic_Latch, out_2);
endmodule

module SRLatch (
  input  in_1,
  input  in_2,
  output Q,
  output out_4
);

  nor nor_1 (Q, in_1, out_4);
  nor nor_2 (out_4, Q, in_2);

  // Notes on the sheet:
  //   Set
  //   Reset
  //   SR Latch
  //   Q
endmodule

module DLatch (
  input  EN,
  input  D,
  output Q,
  output out_4
);

  wire and_1_out, and_2_out, not_1_out;

  not not_1 (not_1_out, D);
  and and_1 (and_1_out, not_1_out, EN);
  and and_2 (and_2_out, EN, D);
  SRLatch srlatch_1 (.in_1(and_1_out), .in_2(and_2_out), .Q(Q), .out_4(out_4));

  // Notes on the sheet:
  //   D Latch
  //   (Data)
  //   (Enable)
  //   Q
endmodule

module DFlipFlop (
  input  D,
  output Q,
  output out_3
);

  wire and_1_out, and_2_out, clock_1_out, not_1_out;

  not not_1 (not_1_out, D);
  Clock #(.lowDuration(8)) clock_1 (.out(clock_1_out));
  and and_1 (and_1_out, not_1_out, clock_1_out);
  and and_2 (and_2_out, clock_1_out, D);
  SRLatch srlatch_1 (.in_1(and_1_out), .in_2(and_2_out), .Q(Q), .out_4(out_3));

  // Notes on the sheet:
  //   D FlipFlop
  //   (Data)
  //   CLK Pulse
  //   Q
endmodule

module ClockPulse (
  output out_1
);

  wire clock_1_out, not_1_out;

  Clock clock_1 (.out(clock_1_out));
  not not_1 (not_1_out, clock_1_out);
  and and_1 (out_1, clock_1_out, not_1_out);
endmodule
