// Logisim project Day11_3bitAdderWithClockAndRegisters.circ as structural Verilog: 4 circuits, main circuit main
module main (
  input  in_1,
  input  in_2,
  input  in_3,
  input  in_4,
  input  in_5,
  output out_6,
  output out_7,
  output out_8,
  output out_9
);

  wire clock_1_out, d_ff_1_q, d_ff_2_q, d_ff_3_q, fulladder_1_out_4, fulladder_1_out_5, fulladder_2_out_4,
       fulladder_2_out_5, fulladder_3_p1, fulladder_3_p4, fulladder_3_p5, halfadder_1_out_3,
       halfadder_1_out_4;

  LED led_1 (.in(in_1));
  LED #(.active("false")) led_2 (.in(in_5));
  LED led_3 (.in(in_5));
  Clock clock_1 (.out(clock_1_out));
  LED led_4 (.in(in_2));
  LED led_5 (.in(in_3));
  LED led_6 (.in(in_4));
  LED led_7 (.in(d_ff_1_q));
  LED led_8 (.in(d_ff_2_q));
  LED led_9 (.in(d_ff_3_q));
  LED led_10 (.in(fulladder_3_p4));
  HalfAdder halfadder_1 (.in_1(in_1), .in_2(d_ff_1_q), .out_3(halfadder_1_out_3), .out_4(halfadder_1_out_4));
  FullAdder fulladder_1 (
    .in_1(halfadder_1_out_4), .in_2(in_2), .in_3(d_ff_2_q), .out_4(fulladder_1_out_4),
    .out_5(fulladder_1_out_5));
  FullAdder fulladder_2 (
    .in_1(fulladder_1_out_5), .in_2(in_3), .in_3(d_ff_3_q), .out_4(fulladder_2_out_4),
    .out_5(fulladder_2_out_5));
  Multiplexer multiplexer_1 (.in0(d_ff_1_q), .in1(halfadder_1_out_3), .out(out_6), .sel(in_5));
  // FullAdder fulladder_3: pin names not known; wires that end beside it: fulladder_3_p1, fulladder_2_out_5, in_4, fulladder_3_p4, fulladder_3_p5
  Multiplexer multiplexer_2 (.in0(d_ff_2_q), .in1(fulladder_1_out_4), .out(out_7), .sel(in_5));
  Multiplexer multiplexer_3 (.in0(d_ff_3_q), .in1(fulladder_2_out_4), .out(out_8), .sel(in_5));
  Multiplexer multiplexer_4 (.in0(fulladder_3_p4), .in1(fulladder_3_p5), .out(out_9), .sel(in_5));
  LED led_11 (.in(out_6));
  LED led_12 (.in(out_7));
  D_Flip_Flop d_ff_1 (.D(out_6), .clk(clock_1_out), .Q(d_ff_1_q));  // open: Qn, preset, reset
  D_Flip_Flop d_ff_2 (.D(out_7), .clk(clock_1_out), .Q(d_ff_2_q));  // open: Qn, preset, reset
  D_Flip_Flop d_ff_3 (.D(out_8), .clk(clock_1_out), .Q(d_ff_3_q));  // open: Qn, preset, reset
  D_Flip_Flop d_ff_4 (.D(out_9), .clk(clock_1_out), .Q(fulladder_3_p4));  // open: Qn, preset, reset
  LED led_13 (.in(out_8));
  LED led_14 (.in(out_9));

  // Notes on the sheet:
  //   Input
  //   Instruction
  //   NOP
  //   ADD
  //   Clock
  //   IN
  //   REG
  //   NOP
  //   ADD
  //   Primitive CPU with 2 Instructions
  //   OUT
  //   Register
  //   Output
endmodule

// HA
module HalfAdder (
  input  in_1,
  input  in_2,
  output out_3,
  output out_4
);

  xor xor_1 (out_3, in_1, in_2);
  and and_1 (out_4, in_1, in_2);
endmodule

// FA
module FullAdder (
  input  in_1,
  input  in_2,
  input  in_3,
  output out_4,
  output out_5
);

  wire halfadder_1_out_3, halfadder_1_out_4, halfadder_2_out_4;

  HalfAdder halfadder_1 (.in_1(in_2), .in_2(in_3), .out_3(halfadder_1_out_3), .out_4(halfadder_1_out_4));
  HalfAdder halfadder_2 (.in_1(in_1), .in_2(halfadder_1_out_3), .out_3(out_4), .out_4(halfadder_2_out_4));
  or or_1 (out_5, halfadder_2_out_4, halfadder_1_out_4);
endmodule

module SevenSegDisplayDecoder (
  input  in_1,
  input  in_2,
  input  b,
  input  in_4,
  output A,
  output out_6,
  output C,
  output D,
  output E,
  output F,
  output G
);

  wire and_1_out, and_2_out, and_3_out, and_4_out, and_5_out, and_6_out, and_7_out, and_8_out, and_9_out,
       and_10_out, and_11_out, and_12_out, and_13_out, and_14_out, and_15_out, and_16_out, and_17_out,
       and_18_out, and_19_out, and_20_out, and_21_out, and_22_out, and_23_out, and_24_out, and_25_out,
       and_26_out, and_27_out, and_28_out, and_29_out, and_30_out, and_31_out, and_32_out, and_33_out,
       not_1_out, not_2_out, not_3_out, not_4_out;

  not not_1 (not_1_out, in_1);
  not not_2 (not_2_out, in_2);
  not not_3 (not_3_out, b);
  not not_4 (not_4_out, in_4);
  and and_1 (and_1_out, not_2_out, not_4_out);
  and and_2 (and_2_out, not_1_out, b);
  and and_3 (and_3_out, in_2, in_4);
  and and_4 (and_4_out, in_1, not_3_out);
  and and_5 (and_5_out, not_3_out, not_4_out);
  and and_6 (and_6_out, not_1_out, b, in_4);
  and and_7 (and_7_out, in_1, not_3_out);
  and and_8 (and_8_out, in_1, not_4_out);
  and and_9 (and_9_out, not_1_out, not_3_out);
  and and_10 (and_10_out, not_1_out, in_2);
  and and_11 (and_11_out, not_2_out, not_3_out);
  and and_12 (and_12_out, in_1, not_2_out);
  and and_13 (and_13_out, in_2, b);
  and and_14 (and_14_out, not_2_out, not_4_out);
  and and_15 (and_15_out, not_1_out, not_2_out, b);
  and and_16 (and_16_out, in_2, not_3_out, in_4);
  and and_17 (and_17_out, not_1_out, b, not_4_out);
  and and_18 (and_18_out, in_1, not_3_out);
  and and_19 (and_19_out, in_1, in_2, in_4);
  and and_20 (and_20_out, not_2_out, not_4_out);
  and and_21 (and_21_out, not_1_out, b, not_4_out);
  and and_22 (and_22_out, in_1, not_3_out, not_4_out);
  and and_23 (and_23_out, not_1_out, in_2, not_3_out);
  and and_24 (and_24_out, in_1, not_2_out, not_3_out);
  and and_25 (and_25_out, in_1, in_2, b);
  and and_26 (and_26_out, not_1_out, not_3_out, not_4_out);
  and and_27 (and_27_out, not_1_out, in_2, not_4_out);
  and and_28 (and_28_out, in_1, not_2_out, not_4_out);
  and and_29 (and_29_out, not_1_out, not_2_out, b);
  and and_30 (and_30_out, in_2, not_3_out);
  and and_31 (and_31_out, in_1, not_3_out);
  and and_32 (and_32_out, in_1, in_2);
  and and_33 (and_33_out, not_1_out, b, not_4_out);
  or or_1 (A, and_1_out, and_2_out, and_3_out, and_4_out);
  or or_2 (out_6, not_2_out, and_5_out, and_6_out, and_7_out, and_8_out);
  or or_3 (C, in_4, and_9_out, and_10_out, and_11_out, and_12_out, and_13_out);
  or or_4 (D, and_14_out, and_15_out, and_16_out, and_17_out, and_18_out, and_19_out);
  or or_5 (E, and_20_out, and_21_out, and_22_out);
  or or_6 (F, and_23_out, and_24_out, and_25_out, and_26_out, and_27_out, and_28_out);
  or or_7 (G, and_29_out, and_30_out, and_31_out, and_32_out, and_33_out);
endmodule
