// Logisim project Day14_ROM.circ as structural Verilog: 5 circuits, main circuit main
module main (
  input  in_1,
  input  in_2,
  input  in_3,
  input  in_4,
  input  in_5,
  input  in_6,
  input  in_7,
  input  in_8,
  output out_9,
  output out_10,
  output out_11,
  output out_12
);

  wire d_ff_1_q, d_ff_2_q, d_ff_3_q, d_ff_4_q, d_ff_5_q, d_ff_6_q, d_ff_7_q, d_ff_8_q, demultiplexer_1_out0,
       demultiplexer_1_out1, demultiplexer_2_out0, demultiplexer_2_out1, demultiplexer_3_out0,
       demultiplexer_3_out1, demultiplexer_4_out0, demultiplexer_4_out1, demultiplexer_5_out0,
       demultiplexer_5_out1, fulladder_1_out_4, fulladder_1_out_5, fulladder_2_out_4, fulladder_2_out_5,
       fulladder_3_p1, fulladder_3_p4, fulladder_3_p5, halfadder_1_out_3, halfadder_1_out_4,
       multiplexer_5_out, multiplexer_6_out, multiplexer_7_out, not_1_out, not_2_out, not_3_out, not_4_out;

  LED led_1 (.in(in_1));
  LED led_2 (.in(in_2));
  LED led_3 (.in(in_3));
  LED led_4 (.in(in_4));
  LED led_5 (.in(multiplexer_5_out));
  LED led_6 (.in(multiplexer_6_out));
  LED led_7 (.in(multiplexer_7_out));
  LED led_8 (.in(fulladder_3_p4));
  not not_1 (not_1_out, multiplexer_5_out);
  not not_2 (not_2_out, multiplexer_6_out);
  not not_3 (not_3_out, multiplexer_7_out);
  not not_4 (not_4_out, fulladder_3_p4);
  HalfAdder halfadder_1 (.in_1(in_1), .in_2(multiplexer_5_out), .out_3(halfadder_1_out_3), .out_4(halfadder_1_out_4));
  FullAdder fulladder_1 (
    .in_1(halfadder_1_out_4), .in_2(in_2), .in_3(multiplexer_6_out), .out_4(fulladder_1_out_4),
    .out_5(fulladder_1_out_5));
  FullAdder fulladder_2 (
    .in_1(fulladder_1_out_5), .in_2(in_3), .in_3(multiplexer_7_out), .out_4(fulladder_2_out_4),
    .out_5(fulladder_2_out_5));
  LED #(.active("false")) led_9 (.in(in_5));
  LED led_10 (.in(in_5));
  LED #(.active("false")) led_11 (.in(in_6));
  LED led_12 (.in(in_6));
  LED #(.active("false")) led_13 (.in(in_8));
  LED led_14 (.in(in_8));
  Multiplexer multiplexer_1 (.in0(not_1_out), .in1(halfadder_1_out_3), .out(out_9), .sel(in_5));
  // FullAdder fulladder_3: pin names not known; wires that end beside it: fulladder_3_p1, fulladder_2_out_5, in_4, fulladder_3_p4, fulladder_3_p5
  Multiplexer multiplexer_2 (.in0(not_2_out), .in1(fulladder_1_out_4), .out(out_10), .sel(in_5));
  Multiplexer multiplexer_3 (.in0(not_3_out), .in1(fulladder_2_out_4), .out(out_11), .sel(in_5));
  Multiplexer multiplexer_4 (.in0(not_4_out), .in1(fulladder_3_p5), .out(out_12), .sel(in_5));
  Demultiplexer demultiplexer_1 (.out0(demultiplexer_1_out0), .out1(demultiplexer_1_out1), .in(out_9), .sel(in_6));
  Demultiplexer demultiplexer_2 (.out0(demultiplexer_2_out0), .out1(demultiplexer_2_out1), .in(in_7), .sel(in_6));
  Demultiplexer demultiplexer_3 (.out0(demultiplexer_3_out0), .out1(demultiplexer_3_out1), .in(out_10), .sel(in_6));
  Demultiplexer demultiplexer_4 (.out0(demultiplexer_4_out0), .out1(demultiplexer_4_out1), .in(out_11), .sel(in_6));
  Demultiplexer demultiplexer_5 (.out0(demultiplexer_5_out0), .out1(demultiplexer_5_out1), .in(out_12), .sel(in_6));
  D_Flip_Flop d_ff_1 (.D(demultiplexer_1_out0), .clk(demultiplexer_2_out0), .Q(d_ff_1_q));  // open: Qn, preset, reset
  D_Flip_Flop d_ff_2 (.D(demultiplexer_3_out0), .clk(demultiplexer_2_out0), .Q(d_ff_2_q));  // open: Qn, preset, reset
  D_Flip_Flop d_ff_3 (.D(demultiplexer_4_out0), .clk(demultiplexer_2_out0), .Q(d_ff_3_q));  // open: Qn, preset, reset
  D_Flip_Flop d_ff_4 (.D(demultiplexer_5_out0), .clk(demultiplexer_2_out0), .Q(d_ff_4_q));  // open: Qn, preset, reset
  LED led_15 (.in(d_ff_1_q));
  LED led_16 (.in(d_ff_2_q));
  LED led_17 (.in(d_ff_3_q));
  LED led_18 (.in(d_ff_4_q));
  D_Flip_Flop d_ff_5 (.D(demultiplexer_1_out1), .clk(demultiplexer_2_out1), .Q(d_ff_5_q));  // open: Qn, preset, reset
  D_Flip_Flop d_ff_6 (.D(demultiplexer_3_out1), .clk(demultiplexer_2_out1), .Q(d_ff_6_q));  // open: Qn, preset, reset
  D_Flip_Flop d_ff_7 (.D(demultiplexer_4_out1), .clk(demultiplexer_2_out1), .Q(d_ff_7_q));  // open: Qn, preset, reset
  D_Flip_Flop d_ff_8 (.D(demultiplexer_5_out1), .clk(demultiplexer_2_out1), .Q(d_ff_8_q));  // open: Qn, preset, reset
  LED led_19 (.in(out_9));
  LED led_20 (.in(out_10));
  LED led_21 (.in(out_11));
  LED led_22 (.in(out_12));
  LED led_23 (.in(d_ff_5_q));
  LED led_24 (.in(d_ff_6_q));
  LED led_25 (.in(d_ff_7_q));
  LED led_26 (.in(d_ff_8_q));
  Multiplexer multiplexer_5 (.in0(d_ff_1_q), .in1(d_ff_5_q), .out(multiplexer_5_out), .sel(in_8));
  Multiplexer multiplexer_6 (.in0(d_ff_2_q), .in1(d_ff_6_q), .out(multiplexer_6_out), .sel(in_8));
  Multiplexer multiplexer_7 (.in0(d_ff_3_q), .in1(d_ff_7_q), .out(multiplexer_7_out), .sel(in_8));
  Multiplexer multiplexer_8 (.in0(d_ff_4_q), .in1(d_ff_8_q), .out(fulladder_3_p4), .sel(in_8));

  // Notes on the sheet:
  //   Input
  //   IN
  //   REG
  //   INV
  //   ADD
  //   Primitive CPU with 2 Instructions and 2 Registers
  //   Instruction
  //   INV
  //   ADD
  //   Dist. Operand
  //   A
  //   B
  //   Source Operand
  //   A
  //   B
  //   Clock
  //   A
  //   Register
  //   B
  //   OUT
  //   Output
endmodule

// HA
module HalfAdder (
  input  in_1,
  input  in_2,
  output out_3,
  output out_4
);

  xor xor_1 (out_3, in_1, in_2);
  and and_1 (out_4, in_1, in_2);
endmodule

// FA
module FullAdder (
  input  in_1,
  input  in_2,
  input  in_3,
  output out_4,
  output out_5
);

  wire halfadder_1_out_3, halfadder_1_out_4, halfadder_2_out_4;

  HalfAdder halfadder_1 (.in_1(in_2), .in_2(in_3), .out_3(halfadder_1_out_3), .out_4(halfadder_1_out_4));
  HalfAdder halfadder_2 (.in_1(in_1), .in_2(halfadder_1_out_3), .out_3(out_4), .out_4(halfadder_2_out_4));
  or or_1 (out_5, halfadder_2_out_4, halfadder_1_out_4);
endmodule

module SevenSegDisplayDecoder (
  input  in_1,
  input  in_2,
  input  b,
  input  in_4,
  output A,
  output out_6,
  output C,
  output D,
  output E,
  output F,
  output G
);

  wire and_1_out, and_2_out, and_3_out, and_4_out, and_5_out, and_6_out, and_7_out, and_8_out, and_9_out,
       and_10_out, and_11_out, and_12_out, and_13_out, and_14_out, and_15_out, and_16_out, and_17_out,
       and_18_out, and_19_out, and_20_out, and_21_out, and_22_out, and_23_out, and_24_out, and_25_out,
       and_26_out, and_27_out, and_28_out, and_29_out, and_30_out, and_31_out, and_32_out, and_33_out,
       not_1_out, not_2_out, not_3_out, not_4_out;

  not not_1 (not_1_out, in_1);
  not not_2 (not_2_out, in_2);
  not not_3 (not_3_out, b);
  not not_4 (not_4_out, in_4);
  and and_1 (and_1_out, not_2_out, not_4_out);
  and and_2 (and_2_out, not_1_out, b);
  and and_3 (and_3_out, in_2, in_4);
  and and_4 (and_4_out, in_1, not_3_out);
  and and_5 (and_5_out, not_3_out, not_4_out);
  and and_6 (and_6_out, not_1_out, b, in_4);
  and and_7 (and_7_out, in_1, not_3_out);
  and and_8 (and_8_out, in_1, not_4_out);
  and and_9 (and_9_out, not_1_out, not_3_out);
  and and_10 (and_10_out, not_1_out, in_2);
  and and_11 (and_11_out, not_2_out, not_3_out);
  and and_12 (and_12_out, in_1, not_2_out);
  and and_13 (and_13_out, in_2, b);
  and and_14 (and_14_out, not_2_out, not_4_out);
  and and_15 (and_15_out, not_1_out, not_2_out, b);
  and and_16 (and_16_out, in_2, not_3_out, in_4);
  and and_17 (and_17_out, not_1_out, b, not_4_out);
  and and_18 (and_18_out, in_1, not_3_out);
  and and_19 (and_19_out, in_1, in_2, in_4);
  and and_20 (and_20_out, not_2_out, not_4_out);
  and and_21 (and_21_out, not_1_out, b, not_4_out);
  and and_22 (and_22_out, in_1, not_3_out, not_4_out);
  and and_23 (and_23_out, not_1_out, in_2, not_3_out);
  and and_24 (and_24_out, in_1, not_2_out, not_3_out);
  and and_25 (and_25_out, in_1, in_2, b);
  and and_26 (and_26_out, not_1_out, not_3_out, not_4_out);
  and and_27 (and_27_out, not_1_out, in_2, not_4_out);
  and and_28 (and_28_out, in_1, not_2_out, not_4_out);
  and and_29 (and_29_out, not_1_out, not_2_out, b);
  and and_30 (and_30_out, in_2, not_3_out);
  and and_31 (and_31_out, in_1, not_3_out);
  and and_32 (and_32_out, in_1, in_2);
  and and_33 (and_33_out, not_1_out, b, not_4_out);
  or or_1 (A, and_1_out, and_2_out, and_3_out, and_4_out);
  or or_2 (out_6, not_2_out, and_5_out, and_6_out, and_7_out, and_8_out);
  or or_3 (C, in_4, and_9_out, and_10_out, and_11_out, and_12_out, and_13_out);
  or or_4 (D, and_14_out, and_15_out, and_16_out, and_17_out, and_18_out, and_19_out);
  or or_5 (E, and_20_out, and_21_out, and_22_out);
  or or_6 (F, and_23_out, and_24_out, and_25_out, and_26_out, and_27_out, and_28_out);
  or or_7 (G, and_29_out, and_30_out, and_31_out, and_32_out, and_33_out);
endmodule

module CustomROM (
  input  in_1,
  input  in_2,
  input  in_3,
  output out_4,
  output out_5,
  output out_6,
  output out_7,
  output out_8,
  output out_9,
  output out_10
);

  wire and_1_out, and_2_out, and_3_out, and_4_out, and_5_out, and_6_out, and_7_out, and_8_out, not_1_out,
       not_2_out, not_3_out, pull_resistor_1_node, pull_resistor_2_node, pull_resistor_3_node,
       pull_resistor_4_node, pull_resistor_5_node, pull_resistor_6_node, pull_resistor_7_node,
       pull_resistor_8_node, pull_resistor_9_node, pull_resistor_10_node, pull_resistor_11_node,
       pull_resistor_12_node, pull_resistor_13_node, pull_resistor_14_node, pull_resistor_15_node,
       pull_resistor_16_node, pull_resistor_17_node, pull_resistor_18_node, pull_resistor_19_node,
       pull_resistor_20_node, pull_resistor_21_node, pull_resistor_22_node, pull_resistor_23_node,
       pull_resistor_24_node, pull_resistor_25_node, pull_resistor_26_node, pull_resistor_27_node,
       pull_resistor_28_node, pull_resistor_29_node, pull_resistor_30_node, pull_resistor_31_node,
       pull_resistor_32_node, pull_resistor_33_node, pull_resistor_34_node, pull_resistor_35_node,
       pull_resistor_36_node, pull_resistor_37_node, pull_resistor_38_node, pull_resistor_39_node,
       pull_resistor_40_node, pull_resistor_41_node, pull_resistor_42_node, pull_resistor_43_node,
       pull_resistor_44_node, pull_resistor_45_node;

  not not_1 (not_1_out, in_1);
  not not_2 (not_2_out, in_2);
  not not_3 (not_3_out, in_3);
  and and_1 (and_1_out, not_1_out, not_2_out, not_3_out);
  and and_2 (and_2_out, not_1_out, not_2_out, in_3);
  and and_3 (and_3_out, not_1_out, in_2, not_3_out);
  and and_4 (and_4_out, not_1_out, in_2, in_3);
  and and_5 (and_5_out, in_1, not_2_out, not_3_out);
  and and_6 (and_6_out, in_1, not_2_out, in_3);
  and and_7 (and_7_out, in_1, in_2, not_3_out);
  and and_8 (and_8_out, in_1, in_2, in_3);
  Pull_Resistor pull_resistor_1 (.node(pull_resistor_1_node));
  Pull_Resistor pull_resistor_2 (.node(pull_resistor_2_node));
  or or_1 (out_4, and_1_out, pull_resistor_1_node, and_3_out, and_4_out, pull_resistor_2_node, pull_resistor_4_node, pull_resistor_5_node, pull_resistor_6_node);
  LED led_1 (.in(out_4));
  Pull_Resistor pull_resistor_3 (.node(pull_resistor_3_node));
  Pull_Resistor pull_resistor_4 (.node(pull_resistor_4_node));
  Pull_Resistor pull_resistor_5 (.node(pull_resistor_5_node));
  Pull_Resistor pull_resistor_6 (.node(pull_resistor_6_node));
  Pull_Resistor pull_resistor_7 (.node(pull_resistor_7_node));
  Pull_Resistor pull_resistor_8 (.node(pull_resistor_8_node));
  Pull_Resistor pull_resistor_9 (.node(pull_resistor_9_node));
  Pull_Resistor pull_resistor_10 (.node(pull_resistor_10_node));
  Pull_Resistor pull_resistor_11 (.node(pull_resistor_11_node));
  Pull_Resistor pull_resistor_12 (.node(pull_resistor_12_node));
  or or_2 (out_5, pull_resistor_3_node, and_2_out, pull_resistor_7_node, pull_resistor_8_node, pull_resistor_9_node, pull_resistor_10_node, pull_resistor_11_node, pull_resistor_12_node);
  LED led_2 (.in(out_5));
  Pull_Resistor pull_resistor_13 (.node(pull_resistor_13_node));
  Pull_Resistor pull_resistor_14 (.node(pull_resistor_14_node));
  Pull_Resistor pull_resistor_15 (.node(pull_resistor_15_node));
  Pull_Resistor pull_resistor_16 (.node(pull_resistor_16_node));
  or or_3 (out_6, pull_resistor_13_node, pull_resistor_14_node, and_3_out, pull_resistor_15_node, pull_resistor_16_node, pull_resistor_19_node, pull_resistor_20_node, pull_resistor_21_node);
  LED led_3 (.in(out_6));
  Pull_Resistor pull_resistor_17 (.node(pull_resistor_17_node));
  Pull_Resistor pull_resistor_18 (.node(pull_resistor_18_node));
  Pull_Resistor pull_resistor_19 (.node(pull_resistor_19_node));
  Pull_Resistor pull_resistor_20 (.node(pull_resistor_20_node));
  Pull_Resistor pull_resistor_21 (.node(pull_resistor_21_node));
  Pull_Resistor pull_resistor_22 (.node(pull_resistor_22_node));
  Pull_Resistor pull_resistor_23 (.node(pull_resistor_23_node));
  Pull_Resistor pull_resistor_24 (.node(pull_resistor_24_node));
  Pull_Resistor pull_resistor_25 (.node(pull_resistor_25_node));
  Pull_Resistor pull_resistor_26 (.node(pull_resistor_26_node));
  Pull_Resistor pull_resistor_27 (.node(pull_resistor_27_node));
  or or_4 (out_7, pull_resistor_17_node, pull_resistor_18_node, pull_resistor_22_node, pull_resistor_23_node, pull_resistor_24_node, pull_resistor_25_node, pull_resistor_26_node, pull_resistor_27_node);
  LED led_4 (.in(out_7));
  Pull_Resistor pull_resistor_28 (.node(pull_resistor_28_node));
  Pull_Resistor pull_resistor_29 (.node(pull_resistor_29_node));
  Pull_Resistor pull_resistor_30 (.node(pull_resistor_30_node));
  Pull_Resistor pull_resistor_31 (.node(pull_resistor_31_node));
  Pull_Resistor pull_resistor_32 (.node(pull_resistor_32_node));
  Pull_Resistor pull_resistor_33 (.node(pull_resistor_33_node));
  or or_5 (out_8, pull_resistor_28_node, pull_resistor_29_node, pull_resistor_30_node, and_4_out, pull_resistor_31_node, pull_resistor_32_node, pull_resistor_33_node, pull_resistor_37_node);
  LED led_5 (.in(out_8));
  Pull_Resistor pull_resistor_34 (.node(pull_resistor_34_node));
  Pull_Resistor pull_resistor_35 (.node(pull_resistor_35_node));
  Pull_Resistor pull_resistor_36 (.node(pull_resistor_36_node));
  Pull_Resistor pull_resistor_37 (.node(pull_resistor_37_node));
  or or_6 (out_9, and_1_out, pull_resistor_34_node, pull_resistor_35_node, and_4_out, pull_resistor_36_node, pull_resistor_39_node, pull_resistor_40_node, pull_resistor_41_node);
  LED led_6 (.in(out_9));
  Pull_Resistor pull_resistor_38 (.node(pull_resistor_38_node));
  Pull_Resistor pull_resistor_39 (.node(pull_resistor_39_node));
  Pull_Resistor pull_resistor_40 (.node(pull_resistor_40_node));
  Pull_Resistor pull_resistor_41 (.node(pull_resistor_41_node));
  Pull_Resistor pull_resistor_42 (.node(pull_resistor_42_node));
  Pull_Resistor pull_resistor_43 (.node(pull_resistor_43_node));
  Pull_Resistor pull_resistor_44 (.node(pull_resistor_44_node));
  Pull_Resistor pull_resistor_45 (.node(pull_resistor_45_node));
  or or_7 (out_10, and_1_out, pull_resistor_38_node, and_3_out, and_4_out, pull_resistor_42_node, pull_resistor_43_node, pull_resistor_44_node, pull_resistor_45_node);
  LED led_7 (.in(out_10));

  // Notes on the sheet:
  //   AND Array
  //   Programmable Logic Devices
  //   Instruction
  //   Dist.
  //   Source
  //   Immediate Value
  //   OR Array
endmodule
