// Logisim project Day2_AND_OR_gates.circ as structural Verilog: 1 circuit, main circuit main
module main (
  input  in_1,
  input  in_2,
  input  in_3,
  input  in_4,
  output out_5,
  output out_6
);

  and AND1 (out_5, in_1, in_2);
  or OR1 (out_6, in_3, in_4);
endmodule
