// Logisim project Day4_HalfAdder.circ as structural Verilog: 2 circuits, main circuit main
module main (
);

  HalfAdder halfadder_1 ();  // open: in_1, in_2, out_3, out_4
endmodule

// HA
module HalfAdder (
  input  in_1,
  input  in_2,
  output out_3,
  output out_4
);

  xor xor_1 (out_3, in_1, in_2);
  and and_1 (out_4, in_1, in_2);
endmodule
