// Logisim project Day5_FullAdder.circ as structural Verilog: 3 circuits, main circuit main
module main (
  input  in_1,
  input  in_2,
  input  in_3,
  input  in_4,
  input  in_5,
  input  in_6,
  input  in_7,
  input  in_8,
  output out_9,
  output out_10,
  output out_11,
  output out_12,
  output out_13
);

  wire fulladder_1_out_5, fulladder_2_out_5, halfadder_1_out_4;

  HalfAdder halfadder_1 (.in_1(in_1), .in_2(in_2), .out_3(out_9), .out_4(halfadder_1_out_4));
  FullAdder fulladder_1 (.in_1(halfadder_1_out_4), .in_2(in_3), .in_3(in_4), .out_4(out_10), .out_5(fulladder_1_out_5));
  FullAdder fulladder_2 (.in_1(fulladder_1_out_5), .in_2(in_5), .in_3(in_6), .out_4(out_11), .out_5(fulladder_2_out_5));
  FullAdder fulladder_3 (.in_1(fulladder_2_out_5), .in_2(in_7), .in_3(in_8), .out_4(out_12), .out_5(out_13));
endmodule

// HA
module HalfAdder (
  input  in_1,
  input  in_2,
  output out_3,
  output out_4
);

  xor xor_1 (out_3, in_1, in_2);
  and and_1 (out_4, in_1, in_2);
endmodule

// FA
module FullAdder (
  input  in_1,
  input  in_2,
  input  in_3,
  output out_4,
  output out_5
);

  wire halfadder_1_out_3, halfadder_1_out_4, halfadder_2_out_4;

  HalfAdder halfadder_1 (.in_1(in_2), .in_2(in_3), .out_3(halfadder_1_out_3), .out_4(halfadder_1_out_4));
  HalfAdder halfadder_2 (.in_1(in_1), .in_2(halfadder_1_out_3), .out_3(out_4), .out_4(halfadder_2_out_4));
  or or_1 (out_5, halfadder_2_out_4, halfadder_1_out_4);
endmodule
