// Logisim project Day9_3bitAdderWith7SegLEDandRegisters.circ as structural Verilog: 4 circuits, main circuit main
module main (
  input  in_1,
  input  in_2,
  input  in_3,
  input  in_4,
  output out_5,
  output out_6,
  output out_7,
  output out_8
);

  wire and_1_out, d_ff_1_q, d_ff_2_q, d_ff_3_q, fulladder_1_out_5, halfadder_1_out_4, or_1_out,
       sevensegdisplaydecoder_1_a, sevensegdisplaydecoder_1_c, sevensegdisplaydecoder_1_d,
       sevensegdisplaydecoder_1_e, sevensegdisplaydecoder_1_f, sevensegdisplaydecoder_1_g,
       sevensegdisplaydecoder_1_out_6, sevensegdisplaydecoder_2_a, sevensegdisplaydecoder_2_c,
       sevensegdisplaydecoder_2_d, sevensegdisplaydecoder_2_e, sevensegdisplaydecoder_2_f,
       sevensegdisplaydecoder_2_g, sevensegdisplaydecoder_2_out_6, sevensegdisplaydecoder_3_a,
       sevensegdisplaydecoder_3_c, sevensegdisplaydecoder_3_d, sevensegdisplaydecoder_3_e,
       sevensegdisplaydecoder_3_f, sevensegdisplaydecoder_3_g, sevensegdisplaydecoder_3_out_6;

  _7_Segment_Display u_7_segment_display_1 (
    .g(sevensegdisplaydecoder_1_g), .f(sevensegdisplaydecoder_1_f), .a(sevensegdisplaydecoder_1_a),
    .b(sevensegdisplaydecoder_1_out_6), .e(sevensegdisplaydecoder_1_e), .d(sevensegdisplaydecoder_1_d),
    .c(sevensegdisplaydecoder_1_c));  // open: dp
  SevenSegDisplayDecoder sevensegdisplaydecoder_1 (
    .in_2(in_3), .b(in_2), .in_4(in_1), .A(sevensegdisplaydecoder_1_a),
    .out_6(sevensegdisplaydecoder_1_out_6), .C(sevensegdisplaydecoder_1_c), .D(sevensegdisplaydecoder_1_d),
    .E(sevensegdisplaydecoder_1_e), .F(sevensegdisplaydecoder_1_f), .G(sevensegdisplaydecoder_1_g));  // open: in_1
  SevenSegDisplayDecoder sevensegdisplaydecoder_2 (
    .in_2(d_ff_3_q), .b(d_ff_2_q), .in_4(d_ff_1_q), .A(sevensegdisplaydecoder_2_a),
    .out_6(sevensegdisplaydecoder_2_out_6), .C(sevensegdisplaydecoder_2_c), .D(sevensegdisplaydecoder_2_d),
    .E(sevensegdisplaydecoder_2_e), .F(sevensegdisplaydecoder_2_f), .G(sevensegdisplaydecoder_2_g));  // open: in_1
  _7_Segment_Display u_7_segment_display_2 (
    .g(sevensegdisplaydecoder_2_g), .f(sevensegdisplaydecoder_2_f), .a(sevensegdisplaydecoder_2_a),
    .b(sevensegdisplaydecoder_2_out_6), .e(sevensegdisplaydecoder_2_e), .d(sevensegdisplaydecoder_2_d),
    .c(sevensegdisplaydecoder_2_c));  // open: dp
  HalfAdder halfadder_1 (.in_1(in_1), .in_2(d_ff_1_q), .out_3(out_5), .out_4(halfadder_1_out_4));
  FullAdder fulladder_1 (
    .in_1(halfadder_1_out_4), .in_2(in_2), .in_3(d_ff_2_q), .out_4(out_6), .out_5(fulladder_1_out_5));
  FullAdder fulladder_2 (.in_1(fulladder_1_out_5), .in_2(in_3), .in_3(d_ff_3_q), .out_4(out_7), .out_5(out_8));
  _7_Segment_Display u_7_segment_display_3 (.b(and_1_out), .c(and_1_out));  // open: g, f, a, e, d, dp
  and and_1 (and_1_out, out_8, or_1_out);
  or or_1 (or_1_out, out_7, out_6);
  SevenSegDisplayDecoder sevensegdisplaydecoder_3 (
    .in_1(out_8), .in_2(out_7), .b(out_6), .in_4(out_5), .A(sevensegdisplaydecoder_3_a),
    .out_6(sevensegdisplaydecoder_3_out_6), .C(sevensegdisplaydecoder_3_c), .D(sevensegdisplaydecoder_3_d),
    .E(sevensegdisplaydecoder_3_e), .F(sevensegdisplaydecoder_3_f), .G(sevensegdisplaydecoder_3_g));
  _7_Segment_Display u_7_segment_display_4 (
    .g(sevensegdisplaydecoder_3_g), .f(sevensegdisplaydecoder_3_f), .a(sevensegdisplaydecoder_3_a),
    .b(sevensegdisplaydecoder_3_out_6), .e(sevensegdisplaydecoder_3_e), .d(sevensegdisplaydecoder_3_d),
    .c(sevensegdisplaydecoder_3_c));  // open: dp
  D_Flip_Flop d_ff_1 (.D(out_5), .clk(in_4), .Q(d_ff_1_q));  // open: Qn, preset, reset
  D_Flip_Flop d_ff_2 (.D(out_6), .clk(in_4), .Q(d_ff_2_q));  // open: Qn, preset, reset
  D_Flip_Flop d_ff_3 (.D(out_7), .clk(in_4), .Q(d_ff_3_q));  // open: Qn, preset, reset
  D_Flip_Flop d_ff_4 (.clk(in_4));  // open: D, Q, Qn, preset, reset

  // Notes on the sheet:
  //   Display
  //   Input
  //   +
  //   3-bit Adder with Registers
  //   =
  //   EN
  //   Storage Register
  //   Output
endmodule

// HA
module HalfAdder (
  input  in_1,
  input  in_2,
  output out_3,
  output out_4
);

  xor xor_1 (out_3, in_1, in_2);
  and and_1 (out_4, in_1, in_2);
endmodule

// FA
module FullAdder (
  input  in_1,
  input  in_2,
  input  in_3,
  output out_4,
  output out_5
);

  wire halfadder_1_out_3, halfadder_1_out_4, halfadder_2_out_4;

  HalfAdder halfadder_1 (.in_1(in_2), .in_2(in_3), .out_3(halfadder_1_out_3), .out_4(halfadder_1_out_4));
  HalfAdder halfadder_2 (.in_1(in_1), .in_2(halfadder_1_out_3), .out_3(out_4), .out_4(halfadder_2_out_4));
  or or_1 (out_5, halfadder_2_out_4, halfadder_1_out_4);
endmodule

module SevenSegDisplayDecoder (
  input  in_1,
  input  in_2,
  input  b,
  input  in_4,
  output A,
  output out_6,
  output C,
  output D,
  output E,
  output F,
  output G
);

  wire and_1_out, and_2_out, and_3_out, and_4_out, and_5_out, and_6_out, and_7_out, and_8_out, and_9_out,
       and_10_out, and_11_out, and_12_out, and_13_out, and_14_out, and_15_out, and_16_out, and_17_out,
       and_18_out, and_19_out, and_20_out, and_21_out, and_22_out, and_23_out, and_24_out, and_25_out,
       and_26_out, and_27_out, and_28_out, and_29_out, and_30_out, and_31_out, and_32_out, and_33_out,
       not_1_out, not_2_out, not_3_out, not_4_out;

  not not_1 (not_1_out, in_1);
  not not_2 (not_2_out, in_2);
  not not_3 (not_3_out, b);
  not not_4 (not_4_out, in_4);
  and and_1 (and_1_out, not_2_out, not_4_out);
  and and_2 (and_2_out, not_1_out, b);
  and and_3 (and_3_out, in_2, in_4);
  and and_4 (and_4_out, in_1, not_3_out);
  and and_5 (and_5_out, not_3_out, not_4_out);
  and and_6 (and_6_out, not_1_out, b, in_4);
  and and_7 (and_7_out, in_1, not_3_out);
  and and_8 (and_8_out, in_1, not_4_out);
  and and_9 (and_9_out, not_1_out, not_3_out);
  and and_10 (and_10_out, not_1_out, in_2);
  and and_11 (and_11_out, not_2_out, not_3_out);
  and and_12 (and_12_out, in_1, not_2_out);
  and and_13 (and_13_out, in_2, b);
  and and_14 (and_14_out, not_2_out, not_4_out);
  and and_15 (and_15_out, not_1_out, not_2_out, b);
  and and_16 (and_16_out, in_2, not_3_out, in_4);
  and and_17 (and_17_out, not_1_out, b, not_4_out);
  and and_18 (and_18_out, in_1, not_3_out);
  and and_19 (and_19_out, in_1, in_2, in_4);
  and and_20 (and_20_out, not_2_out, not_4_out);
  and and_21 (and_21_out, not_1_out, b, not_4_out);
  and and_22 (and_22_out, in_1, not_3_out, not_4_out);
  and and_23 (and_23_out, not_1_out, in_2, not_3_out);
  and and_24 (and_24_out, in_1, not_2_out, not_3_out);
  and and_25 (and_25_out, in_1, in_2, b);
  and and_26 (and_26_out, not_1_out, not_3_out, not_4_out);
  and and_27 (and_27_out, not_1_out, in_2, not_4_out);
  and and_28 (and_28_out, in_1, not_2_out, not_4_out);
  and and_29 (and_29_out, not_1_out, not_2_out, b);
  and and_30 (and_30_out, in_2, not_3_out);
  and and_31 (and_31_out, in_1, not_3_out);
  and and_32 (and_32_out, in_1, in_2);
  and and_33 (and_33_out, not_1_out, b, not_4_out);
  or or_1 (A, and_1_out, and_2_out, and_3_out, and_4_out);
  or or_2 (out_6, not_2_out, and_5_out, and_6_out, and_7_out, and_8_out);
  or or_3 (C, in_4, and_9_out, and_10_out, and_11_out, and_12_out, and_13_out);
  or or_4 (D, and_14_out, and_15_out, and_16_out, and_17_out, and_18_out, and_19_out);
  or or_5 (E, and_20_out, and_21_out, and_22_out);
  or or_6 (F, and_23_out, and_24_out, and_25_out, and_26_out, and_27_out, and_28_out);
  or or_7 (G, and_29_out, and_30_out, and_31_out, and_32_out, and_33_out);
endmodule
